// Logisim project Practica_GomezEmmanuel_Contador_74LS163.circ as structural Verilog: 1 circuit, main circuit main
module main (
  input  P3,
  input  P2,
  input  P1,
  input  P0,
  input  SR,
  input  CEP,
  input  CET,
  input  PE,
  output P0_2,
  output P1_2,
  output P2_2,
  output P3_2,
  output TC
);

  wire and_1_out, CP_out, not_1_out, not_2_out;

  and and_1 (and_1_out, CEP, CET, PE);
  Clock CP (.out(CP_out));
  Counter #(.width(4), .max('hf)) counter_1 (
    .load(not_1_out), .D({P0, P1, P2, P3}), .count(and_1_out), .Q({P3_2, P2_2, P1_2, P0_2}), .carry(TC),
    .clk(CP_out), .clr(not_2_out));
  not not_1 (not_1_out, PE);
  not not_2 (not_2_out, SR);
endmodule
