// Logisim project Practica1(Parte2)_GomezEmmanuel_LeonPablo.circ as structural Verilog: 1 circuit, main circuit main
module main (
);

  wire and_1_out, and_2_out, and_3_out, and_4_out, and_5_out, and_6_out, and_7_out, and_8_out, button_1_out,
       clock_1_out, d_ff_1_q, d_ff_1_qn, d_ff_2_q, d_ff_2_qn, d_ff_3_qn, not_1_out, not_2_out, not_3_out,
       not_4_out, not_5_out, not_6_out, not_7_out, not_8_out, not_9_out, or_1_out, or_2_out;
  wire [0:0] d_ff_4_q;

  not not_1 (not_1_out, d_ff_3_qn);
  not not_2 (not_2_out, d_ff_3_qn);
  not not_3 (not_3_out, button_1_out);
  not not_4 (not_4_out, d_ff_2_q);
  not not_5 (not_5_out, d_ff_1_qn);
  not not_6 (not_6_out, button_1_out);
  not not_7 (not_7_out, d_ff_2_q);
  not not_8 (not_8_out, d_ff_2_q);
  Button button_1 (.out(button_1_out));
  and and_1 (and_1_out, not_2_out, d_ff_1_qn, not_3_out);
  and and_2 (and_2_out, d_ff_3_qn, d_ff_2_q, d_ff_1_qn, button_1_out);
  and and_3 (and_3_out, d_ff_3_qn, not_4_out, not_5_out, not_6_out);
  and and_4 (and_4_out, d_ff_3_qn, d_ff_1_qn, button_1_out);
  and and_5 (and_5_out, d_ff_3_qn, not_7_out, button_1_out);
  and and_6 (and_6_out, not_8_out, d_ff_1_qn, button_1_out);
  not not_9 (not_9_out, button_1_out);
  Clock clock_1 (.out(clock_1_out));
  and and_7 (and_7_out, not_1_out, d_ff_2_q, d_ff_1_qn, button_1_out);
  or or_1 (or_1_out, and_1_out, and_2_out, and_3_out);
  or or_2 (or_2_out, and_4_out, and_5_out, and_6_out);
  D_Flip_Flop d_ff_1 (
    .clk(clock_1_out), .D(and_7_out), .Q(d_ff_1_q), .Qn(d_ff_1_qn), .en(1'b1));  // open: preset, reset
  D_Flip_Flop d_ff_2 (.clk(clock_1_out), .D(or_1_out), .Q(d_ff_2_q), .Qn(d_ff_2_qn), .en(1'b1));  // open: preset, reset
  D_Flip_Flop d_ff_3 (.clk(clock_1_out), .D(or_2_out), .Qn(d_ff_3_qn), .en(1'b1));  // open: Q, preset, reset
  and and_8 (and_8_out, d_ff_1_q, d_ff_2_qn, d_ff_3_qn, not_9_out);
  D_Flip_Flop d_ff_4 (.clk(clock_1_out), .D(and_8_out), .Q(d_ff_4_q[0]), .en(1'b1));  // open: Qn, preset, reset
  Hex_Digit_Display hex_digit_display_1 (.value({3'b000, d_ff_4_q[0]}));  // open: dp
endmodule
