// Logisim project Pract1_GomezEmmanuel.circ as structural Verilog: 1 circuit, main circuit main
module main (
);

  wire and_1_out, and_2_out, and_3_out, and_4_out, and_5_out, and_6_out, button_1_out, clock_1_out, d_ff_1_q,
       d_ff_2_q, d_ff_2_qn, d_ff_3_q, d_ff_3_qn, or_1_out, or_2_out;
  wire [0:0] and_7_out;

  Button button_1 (.out(button_1_out));
  and and_1 (and_1_out, ~d_ff_1_q, d_ff_3_q, ~button_1_out);  // AND_Gate
  and and_2 (and_2_out, ~d_ff_1_q, d_ff_2_q, ~d_ff_3_q, button_1_out);  // AND_Gate
  and and_3 (and_3_out, ~d_ff_1_q, ~d_ff_2_q, button_1_out);  // AND_Gate
  and and_4 (and_4_out, ~d_ff_1_q, ~d_ff_3_q, button_1_out);  // AND_Gate
  and and_5 (and_5_out, ~d_ff_2_q, ~d_ff_3_q, button_1_out);  // AND_Gate
  Clock clock_1 (.out(clock_1_out));
  D_Flip_Flop d_ff_1 (.clk(clock_1_out), .D(and_6_out), .Q(d_ff_1_q), .en(1'b1));  // open: Qn, preset, reset
  and and_6 (and_6_out, ~d_ff_1_q, d_ff_2_q, d_ff_3_q, button_1_out);  // AND_Gate
  D_Flip_Flop d_ff_2 (.clk(clock_1_out), .D(or_1_out), .Q(d_ff_2_q), .Qn(d_ff_2_qn), .en(1'b1));  // open: preset, reset
  or or_1 (or_1_out, and_1_out, and_2_out);
  D_Flip_Flop d_ff_3 (.clk(clock_1_out), .D(or_2_out), .Q(d_ff_3_q), .Qn(d_ff_3_qn), .en(1'b1));  // open: preset, reset
  or or_2 (or_2_out, and_3_out, and_4_out, and_5_out);
  and and_7 (and_7_out[0], d_ff_1_q, d_ff_2_qn, d_ff_3_qn, ~button_1_out);  // AND_Gate
  Hex_Digit_Display hex_digit_display_1 (.value({3'b000, and_7_out[0]}));  // open: dp
endmodule
