// Logisim project Practica1_GomezEmmanuel_1261509.circ as structural Verilog: 1 circuit, main circuit main
module main (
  input  [7:0] in_1,
  input  in_2,
  input  [15:0] in_3,
  input  in_4,
  input  [15:0] in_5,
  input  [15:0] Entrada,
  output [15:0] out_7,
  output [15:0] Salida
);

  wire Clear_out, clock_1_out, clock_2_out, Copiar_de_ROM_a_RAM_out, Escribir_a_RAM_out,
       Lectura_en_Salida_out, nor_1_out, not_1_out, not_2_out, not_3_out, or_1_out;
  wire [15:0] ram_1_data, ram_2_data, register_1_q, rom_1_data;

  nor nor_1 (nor_1_out, in_5[0], in_5[1], in_5[2], in_5[3], in_5[4], in_5[5], in_5[6], in_5[7]);
  not not_1 (not_1_out, nor_1_out);
  Clock clock_1 (.out(clock_1_out));
  RAM #(.dataWidth(16)) ram_1 (.addr(in_1), .data(ram_1_data), .sel(in_2), .clk(clock_1_out), .ld(in_4));  // open: clr
  ROM #(.dataWidth(16)) rom_1 (.addr(in_5[15:8]), .data(rom_1_data), .sel(nor_1_out));
  Register #(.width(16)) register_1 (
    .D(rom_1_data), .en(nor_1_out), .Q(register_1_q), .clk(clock_2_out), .clr(Clear_out));
  RAM #(.dataWidth(16)) ram_2 (
    .addr(in_5[7:0]), .data(ram_2_data), .sel(not_1_out), .clk(clock_2_out), .ld(not_3_out), .clr(Clear_out));
  Button Clear (.out(Clear_out));
  Clock clock_2 (.out(clock_2_out));
  assign out_7 = in_4 ? ram_1_data : 16'bz;  // Controlled_Buffer controlled_buffer_1
  assign ram_1_data = not_2_out ? in_3 : 16'bz;  // Controlled_Buffer controlled_buffer_2
  not not_2 (not_2_out, in_4);
  assign ram_2_data = Lectura_en_Salida_out ? register_1_q : 16'bz;  // Controlled_Buffer controlled_buffer_3
  assign ram_2_data = Copiar_de_ROM_a_RAM_out ? register_1_q : 16'bz;  // Controlled_Buffer controlled_buffer_4
  or or_1 (or_1_out, Copiar_de_ROM_a_RAM_out, Escribir_a_RAM_out);
  not not_3 (not_3_out, or_1_out);
  Button Lectura_en_Salida (.out(Lectura_en_Salida_out));
  Button Copiar_de_ROM_a_RAM (.out(Copiar_de_ROM_a_RAM_out));
  Button Escribir_a_RAM (.out(Escribir_a_RAM_out));
  assign ram_2_data = Escribir_a_RAM_out ? Entrada : 16'bz;  // Controlled_Buffer controlled_buffer_5
  assign Salida = not_3_out ? ram_2_data : 16'bz;  // Controlled_Buffer controlled_buffer_6

  // Notes on the sheet:
  //   ENTRADA
  //   Bus de Direcciones
  //   Bus de Control
  //   contents of rom_1 (hex, n*v repeats v):
  //   a b c d e f aa ab ac ad ae af aaa aab aac aad aaf aaaa aaab aaac aaad aaae aaaf 0 0 7 0 8 8*0 55 5*0
  //   2 7*0 ee 0 0 7 0 0 0 4 4*0 534 0 0 0 6254 0 3 0 2454 0 425 14*0 f 0 54 9*0 aeff 0 0 d 0 5 15*0 2 0 e
  //   0 72 9*0 52 56*0 7 46*0 28
  //   Bus de Datos
endmodule
