// Logisim project PRACT0_GomezEmmanuel_1261509.circ as structural Verilog
module LogicaCombinatoria (
);

  wire button_1_out, clock_1_out, d_ff_1_q, d_ff_2_q, d_ff_2_qn, not_1_out, not_2_out, xor_1_out;
  wire [3:0] or_1_out;

  Clock clock_1 (.out(clock_1_out));
  xor xor_1 (xor_1_out, d_ff_1_q, d_ff_2_q);
  D_Flip_Flop d_ff_1 (
    .clk(clock_1_out), .D(xor_1_out), .Q(d_ff_1_q), .preset(1'b0), .en(1'b1), .reset(button_1_out));  // open: Qn
  D_Flip_Flop d_ff_2 (
    .clk(clock_1_out), .D(d_ff_2_qn), .Q(d_ff_2_q), .Qn(d_ff_2_qn), .preset(1'b0), .en(1'b1),
    .reset(button_1_out));
  Hex_Digit_Display hex_digit_display_1 (.value({or_1_out[3:2], 1'b0, or_1_out[0]}));  // open: dp
  Button button_1 (.out(button_1_out));
  not not_1 (not_1_out, d_ff_1_q);
  not not_2 (not_2_out, d_ff_1_q);
  and and_1 (or_1_out[3], d_ff_1_q, d_ff_2_q);
  and and_2 (or_1_out[2], not_1_out, d_ff_2_q);
  or or_1 (or_1_out[0], not_2_out, d_ff_2_q);
endmodule
