// Logisim project practica3_Registro74LS194.circ as structural Verilog: 5 circuits, main circuit Parte 1
module Parte_1 (
  input  Entrada,
  output out_2
);

  wire and_1_out, and_2_out, and_3_out, and_4_out, and_5_out, and_6_out, and_7_out, clock_1_out, counter_1_q,
       counter_2_q, counter_3_q, not_1_out, not_2_out, not_3_out, not_4_out, not_5_out, or_1_out, or_2_out,
       or_3_out;

  not not_1 (not_1_out, counter_1_q);
  not not_2 (not_2_out, counter_2_q);
  not not_3 (not_3_out, counter_3_q);
  not not_4 (not_4_out, Entrada);
  and and_1 (and_1_out, not_1_out, counter_2_q, counter_3_q, not_4_out);
  and and_2 (and_2_out, counter_1_q, not_2_out, not_3_out, Entrada);
  and and_3 (and_3_out, not_2_out, counter_3_q, Entrada);
  and and_4 (and_4_out, not_1_out, counter_2_q, not_3_out);
  and and_5 (and_5_out, not_2_out, not_3_out, Entrada);
  and and_6 (and_6_out, not_1_out, counter_2_q, not_3_out, not_4_out);
  and and_7 (and_7_out, not_1_out, counter_2_q, counter_3_q, Entrada);
  Clock clock_1 (.out(clock_1_out));
  or or_1 (or_1_out, and_1_out, and_2_out);
  or or_2 (or_2_out, and_3_out, and_4_out);
  or or_3 (or_3_out, and_5_out, and_6_out, and_7_out);
  Counter #(.width(1), .max('h1)) counter_1 (
    .load(1'b1), .D(or_1_out), .count(1'b0), .Q(counter_1_q), .clk(clock_1_out));  // open: carry, clr
  Counter #(.width(1), .max('h1)) counter_2 (
    .load(1'b1), .D(or_2_out), .count(1'b0), .Q(counter_2_q), .clk(clock_1_out));  // open: carry, clr
  Counter #(.width(1), .max('h1)) counter_3 (
    .load(1'b1), .D(or_3_out), .count(1'b0), .Q(counter_3_q), .clk(clock_1_out));  // open: carry, clr
  not not_5 (not_5_out, counter_2_q);
  and and_8 (out_2, counter_1_q, not_5_out, counter_3_q);
endmodule

module _74LS194 (
  input  A,
  input  B,
  input  C,
  input  D,
  input  S1,
  input  S0,
  input  Shift_Right_Serial_Input,
  input  Shift_Left_Serial_Input,
  input  CLK,
  input  CLEAR,
  output QA,
  output QB,
  output QC,
  output QD
);

  wire and_1_out, and_2_out, and_3_out, and_4_out, and_5_out, and_6_out, and_7_out, and_8_out, and_9_out,
       and_10_out, and_11_out, and_12_out, and_13_out, and_14_out, and_15_out, and_16_out, and_17_out,
       nor_1_out, nor_2_out, nor_3_out, nor_4_out, not_1_out, not_2_out, not_3_out, not_4_out, not_5_out,
       not_6_out;

  not not_1 (not_1_out, S1);
  not not_2 (not_2_out, S0);
  and and_1 (and_1_out, Shift_Right_Serial_Input, S1, not_2_out);
  and and_2 (and_2_out, CLK, ~CLEAR);  // AND_Gate
  and and_3 (and_3_out, S0, not_1_out, QB);
  and and_4 (and_4_out, not_2_out, not_1_out, A);
  nor nor_1 (nor_1_out, and_1_out, and_4_out, and_3_out, and_5_out);
  not not_3 (not_3_out, nor_1_out);
  and and_5 (and_5_out, not_2_out, S1, QA);
  S_R_Flip_Flop u_QA (
    .S(not_3_out), .clk(CLK), .R(nor_1_out), .Q(QA), .reset(and_2_out), .en(1'b1));  // open: Qn, preset
  and and_6 (and_6_out, QA, S1, not_2_out);
  and and_7 (and_7_out, not_2_out, not_1_out, B);
  and and_8 (and_8_out, S0, not_1_out, QC);
  and and_9 (and_9_out, S0, S1, QB);
  nor nor_2 (nor_2_out, and_6_out, and_7_out, and_8_out, and_9_out);
  not not_4 (not_4_out, nor_2_out);
  S_R_Flip_Flop u_QB (
    .S(not_4_out), .clk(CLK), .R(nor_2_out), .Q(QB), .reset(and_2_out), .en(1'b1));  // open: Qn, preset
  and and_10 (and_10_out, not_2_out, not_1_out, C);
  and and_11 (and_11_out, QB, S1, not_2_out);
  and and_12 (and_12_out, S0, not_1_out, QD);
  and and_13 (and_13_out, S0, S1, QC);
  nor nor_3 (nor_3_out, and_11_out, and_10_out, and_12_out, and_13_out);
  not not_5 (not_5_out, nor_3_out);
  S_R_Flip_Flop u_QC (
    .S(not_5_out), .clk(CLK), .R(nor_3_out), .Q(QC), .reset(and_2_out), .en(1'b1));  // open: Qn, preset
  and and_14 (and_14_out, QC, S1, not_2_out);
  and and_15 (and_15_out, not_2_out, not_1_out, D);
  nor nor_4 (nor_4_out, and_14_out, and_15_out, and_17_out, and_16_out);
  and and_16 (and_16_out, S0, S1, QD);
  and and_17 (and_17_out, S0, not_1_out, Shift_Left_Serial_Input);
  not not_6 (not_6_out, nor_4_out);
  S_R_Flip_Flop u_QD (
    .S(not_6_out), .clk(CLK), .R(nor_4_out), .Q(QD), .reset(and_2_out), .en(1'b1));  // open: Qn, preset

  // Notes on the sheet:
  //   PARALLEL INPUTS
  //   PARALLEL OUTPUTS
endmodule

module Parte_2 (
  input  CLEAR,
  input  SRSI,
  input  [3:0] PARALLEL_INPUTS,
  input  SLSI,
  input  S1,
  input  S0,
  output [3:0] PARALLEL_OUTPUTS
);

  wire CLK_out;

  _74LS194 u_74ls194_1 (
    .S1(S1), .S0(S0), .Shift_Right_Serial_Input(SRSI), .CLK(CLK_out), .CLEAR(CLEAR),
    .Shift_Left_Serial_Input(SLSI), .A(PARALLEL_INPUTS[3]), .B(PARALLEL_INPUTS[2]), .C(PARALLEL_INPUTS[1]),
    .D(PARALLEL_INPUTS[0]), .QA(PARALLEL_OUTPUTS[3]), .QB(PARALLEL_OUTPUTS[2]), .QC(PARALLEL_OUTPUTS[1]),
    .QD(PARALLEL_OUTPUTS[0]));
  Clock CLK (.out(CLK_out));
endmodule

module Parte_3 (
  output [3:0] out_1
);

  wire and_1_out, and_2_out, and_3_out, and_4_out, and_5_out, and_6_out, clock_1_out, clock_2_out, D0_2_q,
       D0_q, D1_q, not_1_out, or_1_out, or_2_out, or_3_out;

  and and_1 (and_1_out, D0_2_q, ~D1_q, ~D0_q);  // AND_Gate
  and and_2 (and_2_out, ~D0_2_q, D1_q, ~D0_q);  // AND_Gate
  Clock clock_1 (.out(clock_1_out));
  and and_3 (and_3_out, D0_2_q, D1_q, ~D0_q);  // AND_Gate
  or or_1 (or_1_out, and_1_out, and_2_out);
  and and_4 (and_4_out, ~D0_q, ~D0_2_q);  // AND_Gate
  D_Flip_Flop D0 (.clk(clock_1_out), .D(and_3_out), .Q(D0_q), .en(1'b1));  // open: Qn, preset, reset
  D_Flip_Flop D1 (.clk(clock_1_out), .D(or_1_out), .Q(D1_q), .en(1'b1));  // open: Qn, preset, reset
  D_Flip_Flop D0_2 (.clk(clock_1_out), .D(and_4_out), .Q(D0_2_q), .en(1'b1));  // open: Qn, preset, reset
  and and_5 (and_5_out, ~D1_q, D0_2_q);  // AND_Gate
  and and_6 (and_6_out, D0_q, D0_2_q);
  not not_1 (not_1_out, D0_2_q);
  or or_2 (or_2_out, and_5_out, D0_q);
  or or_3 (or_3_out, D1_q, and_6_out);
  _74LS194 u_74ls194_1 (
    .S1(or_2_out), .S0(or_3_out), .Shift_Right_Serial_Input(not_1_out), .CLK(clock_2_out), .CLEAR(1'b1),
    .Shift_Left_Serial_Input(1'b1), .A(1'b0), .B(1'b0), .C(1'b1), .D(1'b1), .QA(out_1[3]), .QB(out_1[2]),
    .QC(out_1[1]), .QD(out_1[0]));
  Clock clock_2 (.out(clock_2_out));
endmodule

module Circuito_Combinatorio (
  input  Q2,
  input  Q1,
  input  Q0,
  output S1,
  output S0,
  output SLSI,
  output SRSI
);

  wire and_1_out, and_2_out, not_1_out;

  not not_1 (not_1_out, Q1);
  and and_1 (and_1_out, Q2, Q0);
  not not_2 (SRSI, Q0);
  and and_2 (and_2_out, not_1_out, Q0);
  or or_1 (S0, Q1, and_1_out);
  or or_2 (S1, and_2_out, Q2);

  assign SLSI = 1'b1;
endmodule
