// Logisim project practica4_GomezEmmanuel.circ as structural Verilog: 3 circuits, main circuit main
module main (
  input  in_1,
  input  in_2,
  output out_3,
  output out_4
);

  wire clock_1_out, clock_2_out;

  Clock clock_1 (.out(clock_1_out));
  Clock clock_2 (.out(clock_2_out));
  Parte1 Parte_1 (.IN(in_1), .OUT(out_3), .CLK(clock_1_out));
  Parte2 Parte_2 (.INPUT(in_2), .OUTPUT(out_4), .CLK(clock_2_out));
endmodule

module Parte1 (
  input  CLK,
  input  IN,
  output OUT
);

  wire [2:0] D0_q;
  wire [3:0] rom_1_data;

  ROM #(.addrWidth(4), .dataWidth(4)) rom_1 (.addr({IN, D0_q}), .data(rom_1_data), .sel(1'b1));
  D_Flip_Flop D2 (.clk(CLK), .D(rom_1_data[2]), .Q(D0_q[2]));  // open: Qn, preset, en, reset
  D_Flip_Flop D1 (.clk(CLK), .D(rom_1_data[1]), .Q(D0_q[1]));  // open: Qn, preset, en, reset
  D_Flip_Flop D0 (.clk(CLK), .D(rom_1_data[0]), .Q(D0_q[0]));  // open: Qn, preset, en, reset
  D_Flip_Flop D_OUT (.clk(CLK), .D(rom_1_data[3]), .Q(OUT));  // open: Qn, preset, en, reset

  // Notes on the sheet:
  //   contents of rom_1 (hex, n*v repeats v):
  //   0 0 3 4 4*0 1 2 2 1 a
endmodule

module Parte2 (
  input  CLK,
  input  INPUT,
  output OUTPUT
);

  wire and_1_out, and_2_out, and_3_out, JK0_qn, JK1_q, or_1_out, xor_1_out;

  and and_1 (and_1_out, JK1_q, INPUT);
  and and_2 (and_2_out, ~INPUT, JK0_qn);  // AND_Gate
  xor xor_1 (xor_1_out, INPUT, JK1_q);
  or or_1 (or_1_out, and_1_out, and_2_out);
  J_K_Flip_Flop JK1 (.J(or_1_out), .clk(CLK), .K(or_1_out), .Q(JK1_q), .en(1'b1));  // open: Qn, preset, reset
  J_K_Flip_Flop JK0 (.J(xor_1_out), .clk(CLK), .K(xor_1_out), .Qn(JK0_qn), .en(1'b1));  // open: Q, preset, reset
  not not_1 (OUTPUT, and_3_out);
  and and_3 (and_3_out, JK1_q, JK0_qn);
endmodule
