// Logisim project Pract1_GomezEmmanuel_1261509.circ as structural Verilog: 2 circuits, main circuit parte1
module parte1 (
  input  [7:0] in_1,
  input  in_2,
  input  [15:0] in_3,
  input  in_4,
  output [15:0] out_5
);

  wire clock_1_out, not_1_out;
  wire [15:0] ram_1_data;

  Clock clock_1 (.out(clock_1_out));
  RAM #(.dataWidth(16)) ram_1 (.addr(in_1), .data(ram_1_data), .sel(in_2), .clk(clock_1_out), .ld(in_4));  // open: clr
  assign out_5 = in_4 ? ram_1_data : 16'bz;  // Controlled_Buffer controlled_buffer_1
  assign ram_1_data = not_1_out ? in_3 : 16'bz;  // Controlled_Buffer controlled_buffer_2
  not not_1 (not_1_out, in_4);
endmodule

module parte2 (
  input  [15:0] in_1,
  input  [15:0] Entrada,
  output [15:0] Salida
);

  wire and_1_out, and_2_out, and_3_out, and_4_out, and_5_out, CLEAR_out, clock_1_out,
       Copiar_de_ROM_a_RAM_out, Escribir_a_RAM_out, Lectura_en_Salida_out;
  wire [15:0] controlled_buffer_3_out, ram_1_data, register_1_q, rom_1_data;

  and and_1 (and_1_out, ~in_1[8], ~in_1[9], ~in_1[10], ~in_1[11], ~in_1[12], ~in_1[13], ~in_1[14], ~in_1[15]);  // AND_Gate
  and and_2 (and_2_out, in_1[8], ~in_1[9], ~in_1[10], ~in_1[11], ~in_1[12], ~in_1[13], ~in_1[14], ~in_1[15]);  // AND_Gate
  and and_3 (and_3_out, and_2_out, and_4_out);
  and and_4 (and_4_out, ~in_1[4], ~in_1[5], ~in_1[6], ~in_1[7]);  // AND_Gate
  ROM #(.dataWidth(16)) rom_1 (.addr(in_1[7:0]), .data(rom_1_data), .sel(and_1_out));
  RAM #(.dataWidth(16)) ram_1 (
    .addr(in_1[7:0]), .data(ram_1_data), .sel(and_3_out), .clk(clock_1_out), .ld(and_5_out), .clr(CLEAR_out));
  Button CLEAR (.out(CLEAR_out));
  Clock clock_1 (.out(clock_1_out));
  Register #(.width(16)) register_1 (
    .D(rom_1_data), .en(and_1_out), .Q(register_1_q), .clk(clock_1_out), .clr(CLEAR_out));
  assign ram_1_data = Copiar_de_ROM_a_RAM_out ? register_1_q : 16'bz;  // Controlled_Buffer controlled_buffer_1
  assign ram_1_data = Escribir_a_RAM_out ? Entrada : 16'bz;  // Controlled_Buffer controlled_buffer_2
  and and_5 (and_5_out, ~Copiar_de_ROM_a_RAM_out, ~Escribir_a_RAM_out);  // AND_Gate
  Button Lectura_en_Salida (.out(Lectura_en_Salida_out));
  assign controlled_buffer_3_out = and_1_out ? register_1_q : 16'bz;  // Controlled_Buffer controlled_buffer_3
  Button Copiar_de_ROM_a_RAM (.out(Copiar_de_ROM_a_RAM_out));
  Button Escribir_a_RAM (.out(Escribir_a_RAM_out));
  assign controlled_buffer_3_out = and_3_out ? ram_1_data : 16'bz;  // Controlled_Buffer controlled_buffer_4
  assign Salida = Lectura_en_Salida_out ? controlled_buffer_3_out : 16'bz;  // Controlled_Buffer controlled_buffer_5
endmodule
