// Logisim project Practica0_GomezEmmanuel_1261509(1).circ as structural Verilog
module LogicaCombinatoria (
);

  wire CLEAR_out, clock_1_out, d_ff_1_q, d_ff_2_q, d_ff_2_qn, xor_1_out;
  wire [3:0] or_1_out;

  xor xor_1 (xor_1_out, d_ff_1_q, d_ff_2_q);
  Clock clock_1 (.out(clock_1_out));
  D_Flip_Flop d_ff_1 (
    .clk(clock_1_out), .D(xor_1_out), .Q(d_ff_1_q), .preset(1'b0), .en(1'b1), .reset(CLEAR_out));  // open: Qn
  D_Flip_Flop d_ff_2 (
    .clk(clock_1_out), .D(d_ff_2_qn), .Q(d_ff_2_q), .Qn(d_ff_2_qn), .preset(1'b0), .en(1'b1),
    .reset(CLEAR_out));
  Button CLEAR (.out(CLEAR_out));
  and and_1 (or_1_out[3], d_ff_1_q, d_ff_2_q);
  and and_2 (or_1_out[2], ~d_ff_1_q, d_ff_2_q);  // AND_Gate
  or or_1 (or_1_out[0], ~d_ff_1_q, d_ff_2_q);  // OR_Gate
  Hex_Digit_Display hex_digit_display_1 (.value({or_1_out[3:2], 1'b0, or_1_out[0]}));  // open: dp
endmodule
