// Logisim project Practica1_GomezEmmanuel_LeonPablo.circ as structural Verilog: 1 circuit, main circuit main
module main (
);

  wire and_1_out, and_2_out, and_3_out, and_4_out, and_5_out, and_6_out, button_1_out, clock_1_out, d_ff_1_q,
       d_ff_2_q, d_ff_2_qn, d_ff_3_q, d_ff_3_qn, not_1_out, not_2_out, not_3_out, not_4_out, not_5_out,
       not_6_out, not_7_out, not_8_out, not_9_out, not_10_out, not_11_out, not_12_out, or_1_out, or_2_out;
  wire [0:0] and_7_out;

  Button button_1 (.out(button_1_out));
  not not_1 (not_1_out, d_ff_1_q);
  not not_2 (not_2_out, d_ff_1_q);
  not not_3 (not_3_out, button_1_out);
  not not_4 (not_4_out, d_ff_1_q);
  not not_5 (not_5_out, d_ff_3_q);
  not not_6 (not_6_out, d_ff_1_q);
  not not_7 (not_7_out, d_ff_2_q);
  not not_8 (not_8_out, d_ff_1_q);
  not not_9 (not_9_out, d_ff_3_q);
  not not_10 (not_10_out, d_ff_2_q);
  not not_11 (not_11_out, d_ff_3_q);
  not not_12 (not_12_out, button_1_out);
  and and_1 (and_1_out, not_2_out, d_ff_3_q, not_3_out);
  and and_2 (and_2_out, not_4_out, d_ff_2_q, not_5_out, button_1_out);
  and and_3 (and_3_out, not_6_out, not_7_out, button_1_out);
  and and_4 (and_4_out, not_8_out, not_9_out, button_1_out);
  and and_5 (and_5_out, not_10_out, not_11_out, button_1_out);
  Clock clock_1 (.out(clock_1_out));
  D_Flip_Flop d_ff_1 (.clk(clock_1_out), .D(and_6_out), .Q(d_ff_1_q), .en(1'b1));  // open: Qn, preset, reset
  and and_6 (and_6_out, not_1_out, d_ff_2_q, d_ff_3_q, button_1_out);
  D_Flip_Flop d_ff_2 (.clk(clock_1_out), .D(or_1_out), .Q(d_ff_2_q), .Qn(d_ff_2_qn), .en(1'b1));  // open: preset, reset
  or or_1 (or_1_out, and_1_out, and_2_out);
  D_Flip_Flop d_ff_3 (.clk(clock_1_out), .D(or_2_out), .Q(d_ff_3_q), .Qn(d_ff_3_qn), .en(1'b1));  // open: preset, reset
  or or_2 (or_2_out, and_3_out, and_4_out, and_5_out);
  and and_7 (and_7_out[0], d_ff_1_q, d_ff_2_qn, d_ff_3_qn, not_12_out);
  Hex_Digit_Display hex_digit_display_1 (.value({3'b000, and_7_out[0]}));  // open: dp
endmodule
