// Logisim project pract2(parte1)_GomezEmmanuel.circ as structural Verilog: 1 circuit, main circuit Moore
module Moore (
  input  Input,
  output Z0,
  output Z1
);

  wire and_1_out, and_2_out, and_3_out, and_4_out, and_5_out, and_6_out, and_7_out, and_8_out, and_9_out,
       and_10_out, and_11_out, CLK_out, d_ff_1_q, d_ff_1_qn, d_ff_2_q, d_ff_2_qn, d_ff_3_q, d_ff_3_qn,
       not_1_out, or_1_out, or_2_out, or_3_out;

  not not_1 (not_1_out, Input);
  and and_1 (and_1_out, d_ff_1_qn, d_ff_2_q, d_ff_3_q);
  and and_2 (and_2_out, d_ff_1_q, d_ff_3_qn, Input);
  and and_3 (and_3_out, d_ff_2_qn, d_ff_3_q, Input);
  and and_4 (and_4_out, d_ff_1_qn, d_ff_2_q, not_1_out);
  and and_5 (and_5_out, d_ff_2_q, d_ff_3_qn, Input);
  and and_6 (and_6_out, d_ff_1_q, d_ff_2_qn, d_ff_3_q);
  and and_7 (and_7_out, d_ff_1_q, d_ff_3_q, Input);
  and and_8 (and_8_out, d_ff_2_qn, d_ff_3_qn, Input);
  and and_9 (and_9_out, d_ff_1_q, d_ff_3_qn, Input);
  and and_10 (and_10_out, d_ff_1_qn, d_ff_2_q, d_ff_3_qn, not_1_out);
  and and_11 (and_11_out, d_ff_1_q, d_ff_2_qn, d_ff_3_q, not_1_out);
  or or_1 (or_1_out, and_1_out, and_2_out);
  Clock CLK (.out(CLK_out));
  or or_2 (or_2_out, and_3_out, and_4_out, and_5_out, and_6_out, and_7_out);
  or or_3 (or_3_out, and_8_out, and_9_out, and_10_out, and_11_out);
  D_Flip_Flop d_ff_1 (.clk(CLK_out), .D(or_1_out), .Q(d_ff_1_q), .Qn(d_ff_1_qn), .en(1'b1));  // open: preset, reset
  D_Flip_Flop d_ff_2 (.clk(CLK_out), .D(or_2_out), .Q(d_ff_2_q), .Qn(d_ff_2_qn), .en(1'b1));  // open: preset, reset
  D_Flip_Flop d_ff_3 (.clk(CLK_out), .D(or_3_out), .Q(d_ff_3_q), .Qn(d_ff_3_qn), .en(1'b1));  // open: preset, reset
  and and_12 (Z0, d_ff_1_q, d_ff_2_qn, d_ff_3_q);
  and and_13 (Z1, d_ff_1_q, d_ff_2_q, d_ff_3_q);

  // Notes on the sheet:
  //   Q2 Q2'
  //   Q0 Q0'
  //   Q1 Q1'
  //   X  X'
  //   Q2 Q2'
  //   Q1 Q1'
  //   Q0 Q0'
endmodule
