// Logisim project pract2(parte2)_GomezEmmanuel.circ as structural Verilog: 1 circuit, main circuit Mealy
module Mealy (
  input  Input,
  output out_2,
  output out_3
);

  wire and_1_out, and_2_out, and_3_out, and_4_out, and_5_out, and_6_out, and_7_out, and_8_out, and_9_out,
       CLK_out, D0_q, D1_q, D2_q, or_1_out, or_2_out;

  and and_1 (and_1_out, D0_q, ~D1_q, Input);  // AND_Gate
  and and_2 (and_2_out, ~D0_q, D1_q, ~D2_q);  // AND_Gate
  and and_3 (and_3_out, ~D0_q, D1_q, Input);  // AND_Gate
  and and_4 (and_4_out, ~D0_q, ~D1_q, Input);  // AND_Gate
  and and_5 (and_5_out, ~D0_q, D1_q, ~D2_q, ~Input);  // AND_Gate
  and and_6 (and_6_out, D0_q, D1_q, ~D2_q, Input);  // AND_Gate
  Clock CLK (.out(CLK_out));
  and and_7 (and_7_out, D0_q, D1_q, ~D2_q);  // AND_Gate
  or or_1 (or_1_out, and_1_out, and_2_out, and_3_out);
  or or_2 (or_2_out, and_4_out, and_5_out, and_6_out);
  D_Flip_Flop D2 (.clk(CLK_out), .D(and_7_out), .Q(D2_q), .en(1'b1));  // open: Qn, preset, reset
  D_Flip_Flop D1 (.clk(CLK_out), .D(or_1_out), .Q(D1_q), .en(1'b1));  // open: Qn, preset, reset
  D_Flip_Flop D0 (.clk(CLK_out), .D(or_2_out), .Q(D0_q), .en(1'b1));  // open: Qn, preset, reset
  and and_8 (and_8_out, D2_q, ~D1_q, D0_q, Input);  // AND_Gate
  and and_9 (and_9_out, D2_q, ~D1_q, ~D0_q, Input);  // AND_Gate
  D_Flip_Flop Z0 (.clk(CLK_out), .D(and_8_out), .Q(out_2), .en(1'b1));  // open: Qn, preset, reset
  D_Flip_Flop Z1 (.clk(CLK_out), .D(and_9_out), .Q(out_3), .en(1'b1));  // open: Qn, preset, reset

  // Notes on the sheet:
  //   D0, D1, D2
  //   Z0
  //   Z1
endmodule
