// Logisim project practica2_GomezEmmanue_LeonPablo.circ as structural Verilog: 3 circuits, main circuit main
module main (
);

  wire CLOCK_out, Input_out, Mealy_out_3, Mealy_out_4, Moore_z0, Moore_z1;

  Button Input (.out(Input_out));
  Clock CLOCK (.out(CLOCK_out));
  Mealy Mealy (.Input(Input_out), .out_3(Mealy_out_3), .out_4(Mealy_out_4), .CLK(CLOCK_out));
  LED Z0 (.in(Mealy_out_3));
  LED Z1 (.in(Mealy_out_4));
  Moore Moore (.Input(Input_out), .Z0(Moore_z0), .Z1(Moore_z1), .CLK(CLOCK_out));
  LED Z0_2 (.in(Moore_z0));
  LED Z1_2 (.in(Moore_z1));
endmodule

module Moore (
  input  Input,
  input  CLK,
  output Z0,
  output Z1
);

  wire and_1_out, and_2_out, and_3_out, and_4_out, and_5_out, and_6_out, and_7_out, and_8_out, and_9_out,
       and_10_out, and_11_out, d_ff_1_q, d_ff_1_qn, d_ff_2_q, d_ff_2_qn, d_ff_3_q, d_ff_3_qn, not_1_out,
       or_1_out, or_2_out, or_3_out;

  not not_1 (not_1_out, Input);
  and and_1 (and_1_out, d_ff_1_qn, d_ff_2_q, d_ff_3_q);
  and and_2 (and_2_out, d_ff_1_q, d_ff_3_qn, Input);
  and and_3 (and_3_out, d_ff_2_qn, d_ff_3_q, Input);
  and and_4 (and_4_out, d_ff_1_qn, d_ff_2_q, not_1_out);
  and and_5 (and_5_out, d_ff_2_q, d_ff_3_qn, Input);
  and and_6 (and_6_out, d_ff_1_q, d_ff_2_qn, d_ff_3_q);
  and and_7 (and_7_out, d_ff_1_q, d_ff_3_q, Input);
  and and_8 (and_8_out, d_ff_2_qn, d_ff_3_qn, Input);
  and and_9 (and_9_out, d_ff_1_q, d_ff_3_qn, Input);
  and and_10 (and_10_out, d_ff_1_qn, d_ff_2_q, d_ff_3_qn, not_1_out);
  and and_11 (and_11_out, d_ff_1_q, d_ff_2_qn, d_ff_3_q, not_1_out);
  or or_1 (or_1_out, and_1_out, and_2_out);
  Clock clock_1 ();  // open: out
  or or_2 (or_2_out, and_3_out, and_4_out, and_5_out, and_6_out, and_7_out);
  or or_3 (or_3_out, and_8_out, and_9_out, and_10_out, and_11_out);
  D_Flip_Flop d_ff_1 (.clk(CLK), .D(or_1_out), .Q(d_ff_1_q), .Qn(d_ff_1_qn), .en(1'b1));  // open: preset, reset
  D_Flip_Flop d_ff_2 (.clk(CLK), .D(or_2_out), .Q(d_ff_2_q), .Qn(d_ff_2_qn), .en(1'b1));  // open: preset, reset
  D_Flip_Flop d_ff_3 (.clk(CLK), .D(or_3_out), .Q(d_ff_3_q), .Qn(d_ff_3_qn), .en(1'b1));  // open: preset, reset
  and and_12 (Z0, d_ff_1_q, d_ff_2_qn, d_ff_3_q);
  and and_13 (Z1, d_ff_1_q, d_ff_2_q, d_ff_3_q);

  // Notes on the sheet:
  //   Q2 Q2'
  //   X  X'
  //   Q0 Q0'
  //   Q1 Q1'
  //   Q2 Q2'
  //   Q1 Q1'
  //   Q0 Q0'
endmodule

module Mealy (
  input  CLK,
  input  Input,
  output out_3,
  output out_4
);

  wire and_1_out, and_2_out, and_3_out, and_4_out, and_5_out, and_6_out, and_7_out, and_8_out, and_9_out,
       D0_q, D1_q, D2_q, or_1_out, or_2_out;

  and and_1 (and_1_out, D0_q, ~D1_q, Input);  // AND_Gate
  and and_2 (and_2_out, ~D0_q, D1_q, ~D2_q);  // AND_Gate
  and and_3 (and_3_out, ~D0_q, D1_q, Input);  // AND_Gate
  and and_4 (and_4_out, ~D0_q, ~D1_q, Input);  // AND_Gate
  and and_5 (and_5_out, ~D0_q, D1_q, ~D2_q, ~Input);  // AND_Gate
  and and_6 (and_6_out, D0_q, D1_q, ~D2_q, Input);  // AND_Gate
  Clock clock_1 ();  // open: out
  and and_7 (and_7_out, D0_q, D1_q, ~D2_q);  // AND_Gate
  or or_1 (or_1_out, and_1_out, and_2_out, and_3_out);
  or or_2 (or_2_out, and_4_out, and_5_out, and_6_out);
  D_Flip_Flop D2 (.clk(CLK), .D(and_7_out), .Q(D2_q), .en(1'b1));  // open: Qn, preset, reset
  D_Flip_Flop D1 (.clk(CLK), .D(or_1_out), .Q(D1_q), .en(1'b1));  // open: Qn, preset, reset
  D_Flip_Flop D0 (.clk(CLK), .D(or_2_out), .Q(D0_q), .en(1'b1));  // open: Qn, preset, reset
  and and_8 (and_8_out, D2_q, ~D1_q, D0_q, Input);  // AND_Gate
  and and_9 (and_9_out, D2_q, ~D1_q, ~D0_q, Input);  // AND_Gate
  D_Flip_Flop Z0 (.clk(CLK), .D(and_8_out), .Q(out_3), .en(1'b1));  // open: Qn, preset, reset
  D_Flip_Flop Z1 (.clk(CLK), .D(and_9_out), .Q(out_4), .en(1'b1));  // open: Qn, preset, reset

  // Notes on the sheet:
  //   D0, D1, D2
  //   Z0
  //   Z1
endmodule
