// Logisim project Practica_GomezEmmanuel_ShiftRegister_74LS194.circ as structural Verilog: 2 circuits, main circuit main
module main (
  input  CLEAR,
  input  Bit_3,
  input  Bit_2,
  input  Bit_1,
  input  Bit_0,
  input  S1,
  input  Shift_Right,
  input  S0
);

  wire CLOCK_out;
  wire [3:0] shift_register_1_bit_0_2;

  Shift_register shift_register_1 (
    .Bit_0(Bit_0), .Bit_1(Bit_1), .Bit_2(Bit_2), .Bit_3(Bit_3), .CLR(CLEAR),
    .Shift_Right_Serial_Input(Shift_Right), .Bit_0_2(shift_register_1_bit_0_2[0]),
    .Bit_1_2(shift_register_1_bit_0_2[1]), .Bit_2_2(shift_register_1_bit_0_2[2]),
    .Bit_3_2(shift_register_1_bit_0_2[3]), .S0(S0), .S1(S1), .CLK(CLOCK_out));
  Hex_Digit_Display hex_digit_display_1 (.value(shift_register_1_bit_0_2));  // open: dp
  Clock CLOCK (.out(CLOCK_out));
endmodule

module Shift_register (
  input  Bit_0,
  input  Bit_1,
  input  Bit_2,
  input  Bit_3,
  input  CLR,
  input  Shift_Right_Serial_Input,
  input  S0,
  input  S1,
  input  CLK,
  output Bit_0_2,
  output Bit_1_2,
  output Bit_2_2,
  output Bit_3_2
);

  wire and_1_out, and_2_out, not_1_out;

  not not_1 (not_1_out, CLR);
  Shift_Register #(.length(4)) shift_register_1 (
    .shift(and_1_out), .in(Shift_Right_Serial_Input), .clk(CLK), .load(and_2_out), .clr(not_1_out),
    .d0(Bit_3), .q0(Bit_3_2), .d1(Bit_2), .q1(Bit_2_2), .d2(Bit_1), .q2(Bit_1_2), .d3(Bit_0), .q3(Bit_0_2));  // open: out
  and and_1 (and_1_out, S0, ~S1);  // AND_Gate
  and and_2 (and_2_out, S0, S1);
endmodule
