// Logisim project Actividad  3.circ as structural Verilog: 1 circuit, main circuit main
module main (
);

  wire dipswitch_1_sw1, dipswitch_1_sw2, dipswitch_1_sw3, dipswitch_1_sw4, dipswitch_1_sw6, dipswitch_1_sw7,
       dipswitch_1_sw8, dipswitch_2_sw1, dipswitch_2_sw2, dipswitch_2_sw3, dipswitch_2_sw4, dipswitch_2_sw5,
       dipswitch_2_sw6, dipswitch_2_sw7, dipswitch_2_sw8, nand_1_out, nand_2_out, nand_3_out, nand_4_out,
       nand_5_out, nand_6_out, nand_7_out, nand_8_out, nand_9_out, nand_10_out, nand_11_out, nand_12_out,
       nand_13_out, nand_14_out, nand_15_out, nand_16_out, nand_17_out, nand_18_out, nand_19_out, nand_20_out;

  nand nand_1 (nand_1_out, dipswitch_1_sw1, dipswitch_1_sw1);
  nand nand_2 (nand_2_out, dipswitch_1_sw2, dipswitch_1_sw2);
  nand nand_3 (nand_3_out, dipswitch_1_sw4, dipswitch_1_sw4);
  nand nand_4 (nand_4_out, dipswitch_1_sw4, dipswitch_1_sw4);
  nand nand_5 (nand_5_out, dipswitch_1_sw3, dipswitch_1_sw3);
  DipSwitch dipswitch_1 (
    .sw1(dipswitch_1_sw1), .sw2(dipswitch_1_sw2), .sw3(dipswitch_1_sw3), .sw4(dipswitch_1_sw4),
    .sw5(dipswitch_1_sw4), .sw6(dipswitch_1_sw6), .sw7(dipswitch_1_sw7), .sw8(dipswitch_1_sw8));
  nand nand_6 (nand_6_out, dipswitch_1_sw7, dipswitch_1_sw7);
  nand nand_7 (nand_7_out, dipswitch_1_sw8, dipswitch_1_sw8);
  nand nand_8 (nand_8_out, dipswitch_1_sw6, dipswitch_1_sw6);
  nand nand_9 (nand_9_out, dipswitch_2_sw1, dipswitch_2_sw1);
  nand nand_10 (nand_10_out, dipswitch_2_sw2, dipswitch_2_sw2);
  nand nand_11 (nand_11_out, dipswitch_2_sw5, dipswitch_2_sw5);
  nand nand_12 (nand_12_out, dipswitch_2_sw3, dipswitch_2_sw3);
  nand nand_13 (nand_13_out, dipswitch_2_sw4, dipswitch_2_sw4);
  DipSwitch dipswitch_2 (
    .sw1(dipswitch_2_sw1), .sw2(dipswitch_2_sw2), .sw3(dipswitch_2_sw3), .sw4(dipswitch_2_sw4),
    .sw5(dipswitch_2_sw5), .sw6(dipswitch_2_sw6), .sw7(dipswitch_2_sw7), .sw8(dipswitch_2_sw8));
  nand nand_14 (nand_14_out, dipswitch_2_sw7, dipswitch_2_sw7);
  nand nand_15 (nand_15_out, dipswitch_2_sw6, dipswitch_2_sw6);
  nand nand_16 (nand_16_out, nand_2_out, nand_4_out, nand_8_out, nand_7_out, nand_10_out, nand_13_out, nand_15_out, nand_20_out);
  nand nand_17 (nand_17_out, nand_5_out, nand_4_out, nand_6_out, nand_7_out, nand_12_out, nand_13_out, nand_14_out, nand_20_out);
  nand nand_18 (nand_18_out, nand_3_out, nand_8_out, nand_6_out, nand_7_out, nand_12_out, nand_11_out, nand_14_out, nand_20_out);
  nand nand_19 (nand_19_out, nand_9_out, nand_10_out, nand_12_out, nand_13_out, nand_11_out, nand_15_out, nand_14_out, nand_20_out);
  nand nand_20 (nand_20_out, dipswitch_2_sw8, dipswitch_2_sw8);
  LED led_1 (.in(nand_16_out));
  LED led_2 (.in(nand_17_out));
  LED led_3 (.in(nand_18_out));
  LED led_4 (.in(nand_19_out));

  // Notes on the sheet:
  //   0 1 2 3 4 5 6 7  8 9 A B C D E F 
endmodule
