// Logisim project Pract2_GomezEmmanuel_01261509.circ as structural Verilog: 3 circuits, main circuit main
module main (
  input  [15:0] Ducto_de_Direcciones,
  input  [15:0] Ducto_de_Datos,
  input  CLEAR,
  input  [15:0] Ducto_de_Datos__Entrada,
  input  [15:0] Ducto_de_Direcciones_2,
  input  CLEAR_2,
  input  [15:0] Escritura,
  output [15:0] Datos__Out,
  output [15:0] Ducto_de_Datos__Salida,
  output [15:0] Lectura
);

  wire CLK_2_out, CLK_out;

  Clock CLK (.out(CLK_out));
  Clock CLK_2 (.out(CLK_2_out));
  Latch__Salida latch_salida_1 (
    ._34CBH(Ducto_de_Direcciones), .Ducto_de_Datos(Ducto_de_Datos), .Salida__OUT(Datos__Out), .CLK(CLK_out),
    .CLEAR(CLEAR));
  Latch__E_S latch_e_s_1 (
    .in_5(Ducto_de_Direcciones_2), .CLK(CLK_2_out), .Entrada(Escritura), .Salida(Lectura),
    .Ducto_de_Datos__Salida(Ducto_de_Datos__Salida), .Ducto_de_Datos__Entrada(Ducto_de_Datos__Entrada),
    .CLEAR(CLEAR_2));

  // Notes on the sheet:
  //   A4FFh Escritura
  //   A7FFh Lectura
  //   Latch (Solo Salida)
  //   Dirección 34CBH
  //   Latch (Entrada/Salida)
endmodule

module Latch__Salida (
  input  [15:0] Ducto_de_Datos,
  input  CLK,
  input  CLEAR,
  input  [15:0] _34CBH,
  output [15:0] Salida__OUT
);

  wire and_1_out, and_2_out;
  wire [15:0] Registro_q;

  and and_1 (and_1_out, _34CBH[0], _34CBH[1], ~_34CBH[2], _34CBH[3], ~_34CBH[4], ~_34CBH[5], _34CBH[6], _34CBH[7]);  // AND_Gate
  and and_2 (and_2_out, ~_34CBH[8], ~_34CBH[9], _34CBH[10], ~_34CBH[11], _34CBH[12], _34CBH[13], ~_34CBH[14], ~_34CBH[15]);  // AND_Gate
  Register #(.width(16)) Registro (.D(Ducto_de_Datos), .en(and_1_out), .Q(Registro_q), .clk(CLK), .clr(CLEAR));
  assign Salida__OUT = and_2_out ? Registro_q : 16'bz;  // Controlled_Buffer controlled_buffer_1

  // Notes on the sheet:
  //   Ducto de Direcciones
  //   Puerto de Latch
  //   IOWRITE
endmodule

module Latch__E_S (
  input  [15:0] Ducto_de_Datos__Entrada,
  input  CLK,
  input  CLEAR,
  input  [15:0] Entrada,
  input  [15:0] in_5,
  output [15:0] Ducto_de_Datos__Salida,
  output [15:0] Salida
);

  wire and_1_out, and_2_out, and_3_out, and_4_out;
  wire [15:0] Registro_q;

  and and_1 (and_1_out, in_5[0], in_5[1], in_5[2], in_5[3], in_5[4], in_5[5], in_5[6], in_5[7]);
  and and_2 (and_2_out, ~in_5[8], ~in_5[9], in_5[10], ~in_5[11], ~in_5[12], in_5[13], ~in_5[14], in_5[15]);  // AND_Gate
  and and_3 (and_3_out, in_5[15], ~in_5[14], in_5[13], ~in_5[12], ~in_5[11], in_5[10], in_5[9], in_5[8]);  // AND_Gate
  and and_4 (and_4_out, and_1_out, and_3_out);
  Register #(.width(16)) Registro (.D(Ducto_de_Datos__Entrada), .en(and_1_out), .Q(Registro_q), .clk(CLK), .clr(CLEAR));
  assign Salida = and_2_out ? Registro_q : 16'bz;  // Controlled_Buffer controlled_buffer_1
  assign Ducto_de_Datos__Salida = and_4_out ? Entrada : 16'bz;  // Controlled_Buffer controlled_buffer_2

  // Notes on the sheet:
  //   A4h Escritura
  //   A7h Lectura
  //   Puerto FFh
  //   Ducto de Direcciones
  //   B34CH Escritura
endmodule
