// Logisim project Pract4_GomezEmmanuel_01261509.circ as structural Verilog: 4 circuits, main circuit Unidad de Ejecucion
module Unidad_de_Ejecucion (
  input  [15:0] Puerto_0,
  input  CLEAR,
  input  in_3,
  output _18h,
  output _3Dh,
  output out_6
);

  wire and_1_out, and_2_out, and_3_out, and_4_out, CAll, clock_1_out, clock_2_out, clock_3_out, clock_4_out,
       clock_5_out, clock_6_out, not_1_out, not_2_out, not_3_out, or_1_out, Reset_Counter_out, S_ADD, S_ALU,
       S_IN, S_INC, S_OUT, S_RAM, S_REGA, S_REGB, S_REGG, START_BUTTON_out;
  wire [2:0] rom_1_data_2;
  wire [3:0] Registro_q_2;
  wire [15:0] alu_1_r, controlled_buffer_1_out, controlled_buffer_2_out, controlled_buffer_3_out,
       controlled_buffer_5_out, controlled_buffer_6_out, controlled_buffer_11_out, COUNTER_out, R0_q, R1_q,
       R2_q, R3_q, REGA_q, REGB_q, Registro_q, rom_1_data;

  Button START_BUTTON (.out(START_BUTTON_out));
  Clock clock_1 (.out(clock_1_out));
  Button Reset_Counter (.out(Reset_Counter_out));
  PROGRAM_COUNTER COUNTER (.IN(START_BUTTON_out), .CLK(clock_1_out), .OUT(COUNTER_out), .CLEAR(Reset_Counter_out));
  ENABLES enables_1 (
    .B2(rom_1_data_2[0]), .B1(rom_1_data_2[1]), .B0(rom_1_data_2[2]), .RAM(S_RAM), .REGG(S_REGG), .IN(S_IN),
    .REGA(S_REGA), .REGB(S_REGB), .ALU(S_ALU), .OUT(S_OUT), .INC(S_INC), .ADD(S_ADD));
  Button Clear_All_Registers (.out(CAll));
  ROM #(.addrWidth(16), .dataWidth(16)) rom_1 (
    .addr(COUNTER_out), .data({rom_1_data[15:8], rom_1_data_2, rom_1_data[4:0]}), .sel(1'b1));
  Clock clock_2 (.out(clock_2_out));
  or or_1 (or_1_out, ~rom_1_data[4], ~rom_1_data[3], ~rom_1_data[2]);  // OR_Gate
  assign controlled_buffer_1_out = S_IN ? Puerto_0 : 16'bz;  // Controlled_Buffer controlled_buffer_1
  RAM #(.addrWidth(16), .dataWidth(16)) ram_1 (
    .addr({{14{1'b0}}, rom_1_data[1:0]}), .data(controlled_buffer_1_out), .sel(S_RAM), .clk(clock_2_out),
    .ld(or_1_out), .clr(CLEAR));
  and and_1 (and_1_out, ~rom_1_data[3], ~rom_1_data[2]);  // AND_Gate
  and and_2 (and_2_out, ~rom_1_data[3], rom_1_data[2]);  // AND_Gate
  and and_3 (and_3_out, rom_1_data[3], ~rom_1_data[2]);  // AND_Gate
  and and_4 (and_4_out, rom_1_data[2], rom_1_data[3]);
  assign controlled_buffer_2_out = S_REGG ? controlled_buffer_1_out : 16'bz;  // Controlled_Buffer controlled_buffer_2
  Register #(.width(16)) R0 (.D(controlled_buffer_2_out), .en(and_1_out), .Q(R0_q), .clk(clock_3_out), .clr(CAll));
  Register #(.width(16)) R1 (.D(controlled_buffer_2_out), .en(and_2_out), .Q(R1_q), .clk(clock_3_out), .clr(CAll));
  Register #(.width(16)) R2 (.D(controlled_buffer_2_out), .en(and_3_out), .Q(R2_q), .clk(clock_3_out), .clr(CAll));
  Register #(.width(16)) R3 (.D(controlled_buffer_2_out), .en(and_4_out), .Q(R3_q), .clk(clock_3_out), .clr(CAll));
  Clock clock_3 (.out(clock_3_out));
  not not_1 (not_1_out, S_REGG);
  assign controlled_buffer_3_out = not_1_out ? controlled_buffer_1_out : 16'bz;  // Controlled_Buffer controlled_buffer_3
  not not_2 (not_2_out, S_ALU);
  assign controlled_buffer_3_out = not_2_out ? controlled_buffer_5_out : 16'bz;  // Controlled_Buffer controlled_buffer_4
  assign controlled_buffer_5_out = S_REGG ? controlled_buffer_6_out : 16'bz;  // Controlled_Buffer controlled_buffer_5
  assign controlled_buffer_6_out = and_1_out ? R0_q : 16'bz;  // Controlled_Buffer controlled_buffer_6
  assign controlled_buffer_6_out = and_2_out ? R1_q : 16'bz;  // Controlled_Buffer controlled_buffer_7
  assign controlled_buffer_6_out = and_3_out ? R2_q : 16'bz;  // Controlled_Buffer controlled_buffer_8
  assign controlled_buffer_6_out = and_4_out ? R3_q : 16'bz;  // Controlled_Buffer controlled_buffer_9
  assign controlled_buffer_3_out = S_ALU ? alu_1_r : 16'bz;  // Controlled_Buffer controlled_buffer_10
  Register #(.width(16)) REGA (.D(controlled_buffer_3_out), .en(S_REGA), .Q(REGA_q), .clk(clock_4_out), .clr(CAll));
  Clock clock_4 (.out(clock_4_out));
  not not_3 (not_3_out, S_REGA);
  Register #(.width(16)) REGB (.D(controlled_buffer_11_out), .en(S_REGB), .Q(REGB_q), .clk(clock_5_out), .clr(CAll));
  assign controlled_buffer_11_out = not_3_out ? controlled_buffer_3_out : 16'bz;  // Controlled_Buffer controlled_buffer_11
  Clock clock_5 (.out(clock_5_out));
  Hex_Digit_Display hex_digit_display_1 (.value(Registro_q[15:12]));  // open: dp
  Register #(.width(16)) Registro (
    .D(REGA_q), .en(S_OUT), .Q({Registro_q[15:8], Registro_q_2, Registro_q[3:0]}), .clk(clock_6_out),
    .clr(CAll));
  Clock clock_6 (.out(clock_6_out));
  ALU alu_1 (
    .A(REGA_q), .B(REGB_q), .Cout(_18h), .Select({S_INC, S_ADD, 2'b00}), .Cin(in_3), .R(alu_1_r),
    .Zero(_3Dh), .Sign_Flag(1'b0), .OverFlow(out_6));
  Hex_Digit_Display hex_digit_display_2 (.value(Registro_q[11:8]));  // open: dp
  Hex_Digit_Display hex_digit_display_3 (.value(Registro_q_2));  // open: dp
  Hex_Digit_Display hex_digit_display_4 (.value(Registro_q[3:0]));  // open: dp

  // Notes on the sheet:
  //   Decodificador de CS
  //   contents of rom_1 (hex, n*v repeats v):
  //   3d 0 41 a7 82 10 30 9 28 a 28 18 4*3d
  //   Registros de Proposito General
  //   3Dh
  //   00h
  //   41h
  //   A7h
  //   82h
  //   10h
  //   30h
  //   09h
  //   28h
  //   Secuencia a realizar
  //   NOP
  //   MOV R0, Mem1
  //   MOV R1Mem2
  //   IN  Mem3, P0
  //   MOV R2, Mem3
  //   MOV A, R0
  //   INC A
  //   MOV B, R1
  //   ADD A, B
  //   ADD R2, B  ->
  //   OUT P1, A
  //   NOP
  //   MOV B, R2
  //   0Ah
  //   28h
  //   ADD A, B
endmodule

module ALU (
  input  [15:0] A,
  input  Cin,
  input  [15:0] B,
  input  Sign_Flag,
  input  [3:0] Select,
  output OverFlow,
  output Cout,
  output Zero,
  output [15:0] R
);

  wire adder_1_cout, adder_2_cout, adder_3_cout, addition, and_1_out, and_2_out, and_3_out, and_4_out,
       and_5_out, and_6_out, and_7_out, and_8_out, and_10_out, and_11_out, and_12_out, and_13_out,
       and_14_out, and_15_out, and_16_out, and_17_out, and_18_out, and_19_out, and_20_out, and_21_out,
       and_22_out, and_23_out, or_4_out, or_5_out, or_6_out, or_7_out, substraction, subtractor_1_bout,
       subtractor_2_bout, subtractor_3_bout;
  wire [15:0] adder_1_out, adder_2_out, adder_3_out, and_9_out, not_1_out, or_2_out, shifter_1_out,
       shifter_2_out, shifter_3_out, shifter_4_out, subtractor_1_out, subtractor_2_out, subtractor_3_out,
       xor_1_out;

  assign Cout = and_1_out ? subtractor_1_bout : 1'bz;  // Controlled_Buffer controlled_buffer_1
  and and_1 (and_1_out, ~Select[3], Select[2], Select[1], Select[0], Select[0]);  // AND_Gate
  assign Cout = and_2_out ? subtractor_2_bout : 1'bz;  // Controlled_Buffer controlled_buffer_2
  and and_2 (and_2_out, ~Select[3], Select[2], Select[1], ~Select[0], ~Select[0]);  // AND_Gate
  and and_3 (and_3_out, Select[3], ~Select[2], ~Select[1], Select[0], Select[0]);  // AND_Gate
  assign Cout = and_6_out ? subtractor_3_bout : 1'bz;  // Controlled_Buffer controlled_buffer_3
  assign Cout = and_7_out ? adder_3_cout : 1'bz;  // Controlled_Buffer controlled_buffer_4
  assign Cout = and_4_out ? adder_1_cout : 1'bz;  // Controlled_Buffer controlled_buffer_5
  and and_4 (and_4_out, ~Select[3], Select[2], ~Select[1], Select[0], Select[0]);  // AND_Gate
  assign Cout = and_8_out ? adder_2_cout : 1'bz;  // Controlled_Buffer controlled_buffer_6
  and and_5 (and_5_out, ~Select[3], Select[2], Select[1], Select[0], Select[0]);  // AND_Gate
  or or_1 (substraction, and_3_out, and_5_out, and_10_out);
  and and_6 (and_6_out, Select[3], ~Select[2], ~Select[1], Select[0], Select[0]);  // AND_Gate
  and and_7 (and_7_out, Select[3], ~Select[2], ~Select[1], ~Select[0], ~Select[0]);  // AND_Gate
  and and_8 (and_8_out, ~Select[3], Select[2], ~Select[1], ~Select[0], ~Select[0]);  // AND_Gate
  assign and_9_out = A & B;  // AND_Gate and_9, 16 bits wide
  and and_10 (and_10_out, ~Select[3], Select[2], Select[1], ~Select[0], ~Select[0]);  // AND_Gate
  and and_11 (and_11_out, Select[3], ~Select[2], ~Select[1], ~Select[0], ~Select[0]);  // AND_Gate
  assign xor_1_out = A ^ B;  // XOR_Gate xor_1, 16 bits wide
  assign or_2_out = A | B;  // OR_Gate or_2, 16 bits wide
  and and_12 (and_12_out, ~Select[3], Select[2], ~Select[1], Select[0], Select[0]);  // AND_Gate
  or or_3 (addition, and_11_out, and_12_out, and_13_out);
  assign not_1_out = ~A;  // NOT_Gate not_1, 16 bits wide
  and and_13 (and_13_out, ~Select[3], Select[2], ~Select[1], ~Select[0], ~Select[0]);  // AND_Gate
  Subtractor #(.width(16)) subtractor_1 (.a(A), .b(B), .out(subtractor_1_out), .bin(Cin), .bout(subtractor_1_bout));
  Subtractor #(.width(16)) subtractor_2 (.a(A), .b(B), .out(subtractor_2_out), .bin(1'b0), .bout(subtractor_2_bout));
  Adder #(.width(16)) adder_1 (.a(A), .b(B), .out(adder_1_out), .cin(Cin), .cout(adder_1_cout));
  Adder #(.width(16)) adder_2 (.a(A), .b(B), .out(adder_2_out), .cin(1'b0), .cout(adder_2_cout));
  // Probe on R
  Multiplexer #(.select(4), .width(16), .enable("false")) multiplexer_1 (
    .in0(and_9_out), .in1(or_2_out), .in2(xor_1_out), .in3(not_1_out), .in4(adder_2_out), .in5(adder_1_out),
    .in6(subtractor_2_out), .in7(subtractor_1_out), .in8(adder_3_out), .in9(subtractor_3_out),
    .in10(shifter_4_out), .in11(shifter_3_out), .in12(shifter_2_out), .in13(shifter_1_out),
    .in14({16{1'b0}}), .in15({16{1'b0}}), .out(R), .sel(Select));
  Shifter #(.width(16), .shift("rr")) shifter_1 (.in(A), .\dist (4'b0001), .out(shifter_1_out));
  Shifter #(.width(16), .shift("rl")) shifter_2 (.in(A), .\dist (4'b0001), .out(shifter_2_out));
  Shifter #(.width(16), .shift("lr")) shifter_3 (.in(A), .\dist (4'b0001), .out(shifter_3_out));
  Shifter #(.width(16)) shifter_4 (.in(A), .\dist (4'b0001), .out(shifter_4_out));
  Subtractor #(.width(16)) subtractor_3 (
    .a(A), .b(16'h1), .out(subtractor_3_out), .bin(1'b0), .bout(subtractor_3_bout));
  Adder #(.width(16)) adder_3 (.a(A), .b(16'h1), .out(adder_3_out), .cin(1'b0), .cout(adder_3_cout));
  and and_14 (and_14_out, ~A[15], ~B[15], R[15]);  // AND_Gate
  or or_4 (or_4_out, and_14_out, and_15_out);
  and and_15 (and_15_out, A[15], B[15], ~R[15]);  // AND_Gate
  and and_16 (and_16_out, ~A[15], B[15], R[15]);  // AND_Gate
  or or_5 (or_5_out, and_16_out, and_17_out);
  and and_17 (and_17_out, A[15], ~R[15]);  // AND_Gate
  nor nor_1 (Zero, R[0], R[1], R[2], R[3], R[4], R[5], R[6], R[7], R[8], R[9], R[10], R[11], R[12], R[13], R[14], R[15]);
  and and_18 (and_18_out, or_4_out, Sign_Flag);
  or or_6 (or_6_out, and_18_out, and_19_out);
  and and_19 (and_19_out, ~Sign_Flag, Cout);  // AND_Gate
  and and_20 (and_20_out, or_5_out, Sign_Flag);
  or or_7 (or_7_out, and_20_out, and_21_out);
  and and_21 (and_21_out, ~Sign_Flag, Cout);  // AND_Gate
  and and_22 (and_22_out, or_6_out, addition);
  and and_23 (and_23_out, or_7_out, substraction);
  or or_8 (OverFlow, and_22_out, and_23_out);

  // Other names for the same wires on the sheet: A_t = A[15]; B_t = B[15]; R_t = R[15]; SF = Sign_Flag

  // Notes on the sheet:
  //   Tabla de Funciones
  //   0000 -- A and B
  //   0001 -- A or B
  //   0010 -- A xor B
  //   0011 -- not A
  //   0100 -- A add B
  //   0101 -- A adc B
  //   0110 -- A sub B
  //   0111 -- A sbb B
  //   1000 -- inc A
  //   1001 -- dec A
  //   1010 -- shl A
  //   1011 --  shr A
  //   1100 -- rol A
  //   1101 -- ror A
endmodule

module ENABLES (
  input  B2,
  input  B1,
  input  B0,
  output RAM,
  output REGG,
  output IN,
  output REGA,
  output REGB,
  output ALU,
  output OUT,
  output INC,
  output ADD
);

  wire and_2_out, and_3_out, and_5_out, and_6_out, and_7_out, and_9_out, and_10_out;

  and and_1 (RAM, ~B2, ~B1);  // AND_Gate
  and and_2 (and_2_out, ~B2, ~B0);  // AND_Gate
  and and_3 (and_3_out, ~B1, ~B0);  // AND_Gate
  and and_4 (IN, ~B2, ~B1, B0);  // AND_Gate
  and and_5 (and_5_out, ~B2, B1);  // AND_Gate
  and and_6 (and_6_out, B1, ~B0);  // AND_Gate
  and and_7 (and_7_out, B2, ~B1, B0);  // AND_Gate
  and and_8 (REGB, B2, ~B1);  // AND_Gate
  and and_9 (and_9_out, ~B2, B1, B0);  // AND_Gate
  and and_10 (and_10_out, B2, ~B1, B0);  // AND_Gate
  and and_11 (OUT, B2, B1, ~B0);  // AND_Gate
  and and_12 (INC, ~B2, B1, B0);  // AND_Gate
  and and_13 (ADD, B0, ~B1, B2);  // AND_Gate
  or or_1 (REGG, and_2_out, and_3_out);
  or or_2 (REGA, and_5_out, and_6_out, and_7_out);
  or or_3 (ALU, and_9_out, and_10_out);
endmodule

module PROGRAM_COUNTER (
  input  IN,
  input  CLK,
  input  CLEAR,
  output [15:0] OUT
);

  wire and_1_out, and_2_out, and_3_out, and_4_out, and_5_out, and_6_out, and_7_out, and_8_out, and_9_out,
       and_10_out, and_11_out, and_12_out, and_13_out, and_14_out, or_1_out, or_2_out, or_3_out, or_4_out;

  and and_1 (and_1_out, ~OUT[3], OUT[2], OUT[1], OUT[0]);  // AND_Gate
  or or_1 (or_1_out, and_1_out, and_2_out, and_3_out);
  and and_2 (and_2_out, OUT[3], ~OUT[2], ~OUT[1]);  // AND_Gate
  and and_3 (and_3_out, OUT[3], ~OUT[2], ~OUT[0]);  // AND_Gate
  and and_4 (and_4_out, ~OUT[3], ~OUT[2], OUT[1], OUT[0]);  // AND_Gate
  and and_5 (and_5_out, ~OUT[3], OUT[2], ~OUT[1]);  // AND_Gate
  or or_2 (or_2_out, and_4_out, and_5_out, and_6_out);
  and and_6 (and_6_out, ~OUT[3], OUT[2], ~OUT[0]);  // AND_Gate
  and and_7 (and_7_out, ~OUT[3], ~OUT[1], OUT[0]);  // AND_Gate
  and and_8 (and_8_out, ~OUT[2], ~OUT[1], OUT[0]);  // AND_Gate
  or or_3 (or_3_out, and_7_out, and_8_out, and_9_out, and_10_out);
  and and_9 (and_9_out, ~OUT[3], OUT[1], ~OUT[0]);  // AND_Gate
  and and_10 (and_10_out, ~OUT[2], OUT[1], ~OUT[0]);  // AND_Gate
  and and_11 (and_11_out, ~OUT[3], OUT[1], ~OUT[0]);  // AND_Gate
  and and_12 (and_12_out, ~OUT[3], OUT[2], ~OUT[0]);  // AND_Gate
  or or_4 (or_4_out, and_11_out, and_12_out, and_13_out, and_14_out);
  and and_13 (and_13_out, OUT[3], ~OUT[2], ~OUT[0]);  // AND_Gate
  and and_14 (and_14_out, IN, ~OUT[3], ~OUT[0]);  // AND_Gate
  D_Flip_Flop d_ff_1 (.clk(CLK), .D(or_1_out), .Q(OUT[3]), .en(1'b1), .reset(CLEAR));  // open: Qn, preset
  D_Flip_Flop d_ff_2 (.clk(CLK), .D(or_2_out), .Q(OUT[2]), .en(1'b1), .reset(CLEAR));  // open: Qn, preset
  D_Flip_Flop d_ff_3 (.clk(CLK), .D(or_3_out), .Q(OUT[1]), .en(1'b1), .reset(CLEAR));  // open: Qn, preset
  D_Flip_Flop d_ff_4 (.clk(CLK), .D(or_4_out), .Q(OUT[0]), .en(1'b1), .reset(CLEAR));  // open: Qn, preset

  assign OUT[15:4] = {12{1'b0}};
endmodule
