// Logisim project practica3_GomezEmmanuel_01261509.circ as structural Verilog: 2 circuits, main circuit Main
module Main (
  input  [7:0] A,
  input  [7:0] B,
  input  Cin,
  input  Sign_Flag,
  input  [3:0] Funcion,
  output Cout,
  output Zero,
  output OverFlow,
  output [7:0] Resultado
);

  ALU alu_1 (
    .A(A), .B(B), .Cout(Cout), .Select(Funcion), .Cin(Cin), .R(Resultado), .Zero(Zero), .OverFlow(OverFlow),
    .Sign_Flag(Sign_Flag));

  // Notes on the sheet:
  //   0000 -- A and B
  //   0001 -- A or B
  //   0010 -- A xor B
  //   0011 -- not A
  //   0101 -- A adc B
  //   Tabla de Funciones
  //   0100 -- A add B
  //   0110 -- A sub B
  //   0111 -- A sbb B
  //   1000 -- inc A
  //   1001 -- dec A
  //   1010 -- shl A
  //   1011 --  shr A
  //   1100 -- rol A
  //   1101 -- ror A
endmodule

module ALU (
  input  [7:0] A,
  input  Cin,
  input  [7:0] B,
  input  Sign_Flag,
  input  [3:0] Select,
  output Cout,
  output OverFlow,
  output Zero,
  output [7:0] R
);

  wire adder_1_cout, adder_2_cout, adder_3_cout, and_1_out, and_2_out, and_3_out, and_4_out, and_5_out,
       and_6_out, and_7_out, and_8_out, and_10_out, and_11_out, and_12_out, and_13_out, and_14_out,
       and_15_out, and_16_out, and_17_out, Ctrl, CtrlResta, or_4_out, or_5_out, subtractor_1_bout,
       subtractor_2_bout, subtractor_3_bout, xor_2_out;
  wire [7:0] adder_1_out, adder_2_out, adder_3_out, and_9_out, not_1_out, or_3_out, shifter_1_out,
       shifter_2_out, shifter_3_out, shifter_4_out, subtractor_1_out, subtractor_2_out, subtractor_3_out,
       xor_1_out;

  assign Cout = and_1_out ? subtractor_1_bout : 1'bz;  // Controlled_Buffer controlled_buffer_1
  and and_1 (and_1_out, ~Select[3], Select[2], Select[1], Select[0], Select[0]);  // AND_Gate
  assign Cout = and_2_out ? subtractor_2_bout : 1'bz;  // Controlled_Buffer controlled_buffer_2
  and and_2 (and_2_out, ~Select[3], Select[2], Select[1], ~Select[0], ~Select[0]);  // AND_Gate
  and and_3 (and_3_out, Select[3], ~Select[2], ~Select[1], Select[0], Select[0]);  // AND_Gate
  assign Cout = and_6_out ? subtractor_3_bout : 1'bz;  // Controlled_Buffer controlled_buffer_3
  assign Cout = and_7_out ? adder_3_cout : 1'bz;  // Controlled_Buffer controlled_buffer_4
  assign Cout = and_4_out ? adder_1_cout : 1'bz;  // Controlled_Buffer controlled_buffer_5
  and and_4 (and_4_out, ~Select[3], Select[2], ~Select[1], Select[0], Select[0]);  // AND_Gate
  assign Cout = and_8_out ? adder_2_cout : 1'bz;  // Controlled_Buffer controlled_buffer_6
  and and_5 (and_5_out, ~Select[3], Select[2], Select[1], Select[0], Select[0]);  // AND_Gate
  or or_1 (CtrlResta, and_3_out, and_5_out, and_10_out);
  and and_6 (and_6_out, Select[3], ~Select[2], ~Select[1], Select[0], Select[0]);  // AND_Gate
  and and_7 (and_7_out, Select[3], ~Select[2], ~Select[1], ~Select[0], ~Select[0]);  // AND_Gate
  and and_8 (and_8_out, ~Select[3], Select[2], ~Select[1], ~Select[0], ~Select[0]);  // AND_Gate
  assign and_9_out = A & B;  // AND_Gate and_9, 8 bits wide
  and and_10 (and_10_out, ~Select[3], Select[2], Select[1], ~Select[0], ~Select[0]);  // AND_Gate
  and and_11 (and_11_out, Select[3], ~Select[2], ~Select[1], ~Select[0], ~Select[0]);  // AND_Gate
  or or_2 (Ctrl, CtrlResta, or_4_out);
  assign xor_1_out = A ^ B;  // XOR_Gate xor_1, 8 bits wide
  assign or_3_out = A | B;  // OR_Gate or_3, 8 bits wide
  and and_12 (and_12_out, ~Select[3], Select[2], ~Select[1], Select[0], Select[0]);  // AND_Gate
  or or_4 (or_4_out, and_11_out, and_12_out, and_13_out);
  assign not_1_out = ~A;  // NOT_Gate not_1, 8 bits wide
  and and_13 (and_13_out, ~Select[3], Select[2], ~Select[1], ~Select[0], ~Select[0]);  // AND_Gate
  Subtractor subtractor_1 (.a(A), .b(B), .out(subtractor_1_out), .bin(Cin), .bout(subtractor_1_bout));
  Subtractor subtractor_2 (.a(A), .b(B), .out(subtractor_2_out), .bin(1'b0), .bout(subtractor_2_bout));
  Adder adder_1 (.a(A), .b(B), .out(adder_1_out), .cin(Cin), .cout(adder_1_cout));
  Adder adder_2 (.a(A), .b(B), .out(adder_2_out), .cin(1'b0), .cout(adder_2_cout));
  Multiplexer #(.select(4), .width(8), .enable("false")) multiplexer_1 (
    .in0(and_9_out), .in1(or_3_out), .in2(xor_1_out), .in3(not_1_out), .in4(adder_2_out), .in5(adder_1_out),
    .in6(subtractor_2_out), .in7(subtractor_1_out), .in8(adder_3_out), .in9(subtractor_3_out),
    .in10(shifter_4_out), .in11(shifter_3_out), .in12(shifter_2_out), .in13(shifter_1_out), .in14({8{1'b0}}),
    .in15({8{1'b0}}), .out(R), .sel(Select));
  Shifter #(.shift("rr")) shifter_1 (.in(A), .\dist (3'b001), .out(shifter_1_out));
  Shifter #(.shift("rl")) shifter_2 (.in(A), .\dist (3'b001), .out(shifter_2_out));
  Shifter #(.shift("lr")) shifter_3 (.in(A), .\dist (3'b001), .out(shifter_3_out));
  Shifter shifter_4 (.in(A), .\dist (3'b001), .out(shifter_4_out));
  Subtractor subtractor_3 (.a(A), .b(8'h1), .out(subtractor_3_out), .bin(1'b0), .bout(subtractor_3_bout));
  Adder adder_3 (.a(A), .b(8'h1), .out(adder_3_out), .cin(1'b0), .cout(adder_3_cout));
  nor nor_1 (Zero, R[0], R[1], R[2], R[3], R[3], R[4], R[5], R[6], R[7]);
  xor xor_2 (xor_2_out, B[7], CtrlResta);
  and and_14 (and_14_out, ~A[7], Ctrl, ~xor_2_out, R[7]);  // AND_Gate
  and and_15 (and_15_out, ~R[7], A[7], xor_2_out, Ctrl);  // AND_Gate
  or or_5 (or_5_out, and_14_out, and_15_out);
  and and_16 (and_16_out, or_5_out, Sign_Flag);
  and and_17 (and_17_out, ~Sign_Flag, Ctrl, Cout);  // AND_Gate
  or or_6 (OverFlow, and_16_out, and_17_out);

  // Notes on the sheet:
  //   Tabla de Funciones
  //   0000 -- A and B
  //   0001 -- A or B
  //   0010 -- A xor B
  //   0011 -- not A
  //   0100 -- A add B
  //   0101 -- A adc B
  //   0110 -- A sub B
  //   0111 -- A sbb B
  //   1000 -- inc A
  //   1001 -- dec A
  //   1010 -- shl A
  //   1011 --  shr A
  //   1100 -- rol A
  //   1101 -- ror A
endmodule
